# Fritzing sketch Proyecto LY2 (saved by Fritzing 0.9.3b)
breadboards: 2

parts:
  U1 = ESP32-30Pin [part_number=ESP32-30Pin]
  S1 = Pushbutton [package="[THT]"]
  S2 = Pushbutton [package="[THT]"]
  S3 = Pushbutton [package="[THT]"]
  S4 = Pushbutton [package="[THT]"]
  S5 = Pushbutton [package="[THT]"]
  S6 = Pushbutton [package="[THT]"]
  S7 = Pushbutton [package="[THT]"]
  R1 = Resistor [tolerance=±5% resistance=220 package=THT]
  R2 = Resistor [tolerance=±5% resistance=220 package=THT]
  R3 = Resistor [tolerance=±5% resistance=220 package=THT]
  R5 = Resistor [tolerance=±5% resistance=220 package=THT]
  R6 = Resistor [tolerance=±5% resistance=220 package=THT]
  R7 = Resistor [tolerance=±5% resistance=220 package=THT]
  R8 = Resistor [tolerance=±5% resistance=220 package=THT]
  LED1 = LED - 5mm [color="Blue (470nm)" package="5 mm [THT]"]
  J1 = Piezo Speaker
  LED2 = LED - 5mm [color="Green (555nm)" package="5 mm [THT]"]
  LED3 = LED - 5mm [color="Yellow (585nm)" package="5 mm [THT]"]
  LED4 = LED - 5mm [color="Red (660nm)" package="5 mm [THT]"]
  LED5 = LED - 5mm [color="Orange (620nm)" package="5 mm [THT]"]
  LED6 = LED - 5mm [color="Blue (525nm)" package="5 mm [THT]"]
  LED7 = LED - 5mm [color="Infrared (880nm)" package="5 mm [THT]"]
  LED8 = LED - 5mm [color="Blue (470nm)" package="5 mm [THT]"]
  R9 = Resistor [tolerance=±5% resistance=220 package=THT]
  R10 = Resistor [tolerance=±5% resistance=220 package=THT]
  R11 = Resistor [tolerance=±5% resistance=220 package=THT]
  R12 = Resistor [tolerance=±5% resistance=220 package=THT]
  R13 = Resistor [tolerance=±5% resistance=220 package=THT]
  R14 = Resistor [tolerance=±5% resistance=220 package=THT]
  R15 = Resistor [tolerance=±5% resistance=220 package=THT]
  R16 = Resistor [tolerance=±5% resistance=220 package=THT]
  S8 = Pushbutton [package="[THT]"]

nets:
  N1: U1.3v3, S1.Pin_3, S1.Pin_4, S2.Pin_3, S2.Pin_4, S3.Pin_3, S3.Pin_4, S4.Pin_3, S4.Pin_4, S5.Pin_3, S5.Pin_4, S6.Pin_3, S6.Pin_4, S7.Pin_3, S7.Pin_4, R1.Pin_0, R2.Pin_0, R3.Pin_0, R5.Pin_0, R6.Pin_0, R7.Pin_0, R8.Pin_0, S8.Pin_3, S8.Pin_4
  N2: U1.GND#16, LED1.cathode, J1.pin1, LED2.cathode, LED3.cathode, LED4.cathode, LED5.cathode, LED6.cathode, LED7.cathode, LED8.cathode
  N3: U1.D15, S1.Pin_1, S1.Pin_2, R1.Pin_1, R9.Pin_0
  N4: U1.D2, S2.Pin_1, S2.Pin_2, R2.Pin_1, R10.Pin_0
  N5: U1.D4, S3.Pin_1, S3.Pin_2, R3.Pin_1, R11.Pin_0
  N6: U1.D5, S4.Pin_1, S4.Pin_2, R12.Pin_0
  N7: U1.D18, S5.Pin_1, S5.Pin_2, R5.Pin_1, R13.Pin_0
  N8: U1.D19, S6.Pin_1, S6.Pin_2, R6.Pin_1, R14.Pin_0
  N9: U1.D21, S7.Pin_1, S7.Pin_2, R7.Pin_1, R15.Pin_0
  N10: U1.D22, R8.Pin_1, R16.Pin_0, S8.Pin_1, S8.Pin_2
  N11: U1.D23, J1.pin2
  N12: LED1.anode, R9.Pin_1
  N13: LED2.anode, R10.Pin_1
  N14: LED3.anode, R11.Pin_1
  N15: LED4.anode, R12.Pin_1
  N16: LED5.anode, R13.Pin_1
  N17: LED6.anode, R14.Pin_1
  N18: LED7.anode, R15.Pin_1
  N19: LED8.anode, R16.Pin_1

custom parts:
  ESP32-30Pin: Generic 30-Pin ESP32
